# Fritzing sketch shema_elec (saved by Fritzing 0.9.3b)

parts:
  Composant1 = Lilypad Power Supply
  Composant2 = Arduino Nano (Rev3.0) (ICSP)
  M1 = Dagu DGServo 9g (Pan and tilt) [part_number=RS001B]  # not connected
  M2 = Dagu DGServo 9g (Pan and tilt) [part_number=RS001B]  # not connected
  M3 = Dagu DGServo 9g (Pan and tilt) [part_number=RS001B]  # not connected
  M4 = Dagu DGServo 9g (Pan and tilt) [part_number=RS001B]  # not connected

nets:
  N1: Composant1.+, Composant2.5V
  GND: Composant1.GND, Composant2.VIN, Composant2.GND
